# Fritzing sketch Overview (saved by Fritzing 0.9.3b)
breadboards: 2

parts:
  Part1 = Triple Axis Accelerometer Breakout - ADXL335  # not connected
  Part2 = Arduino Uno (Rev3)  # not connected
  GY-NEO6MV3 = SUP500F [package=sup500f]
  M1 = sim800L v2 evb  # not connected
  Part3 = Arduino Motor Shield  # not connected
  L8 = Inductor [package="400 mil [THT]"]
  L9 = Inductor [package="400 mil [THT]"]
  L10 = Inductor [package="400 mil [THT]"]
  L11 = Inductor [package="400 mil [THT]"]
  L12 = Inductor [package="400 mil [THT]"]
  L13 = Inductor [package="400 mil [THT]"]
  L14 = Inductor [package="400 mil [THT]"]
  S3 = Reed switch [package=THT]
  VCC2 = Battery
  PWR1 = LED - 5mm [color="Blue (430nm)" current=0.030 package="5 mm [THT]"]
  S4 = Toggle Switch [package=THT]
  R2 = Resistor [resistance=220 tolerance=±5% power=0.25 package=THT]
  SENSITIVITY1 = Rotary Potentiometer (Large) [maximum_resistance=100kΩ package=THT]
  LED7 = LED - 5mm [color="Red (633nm)" current=0.030 package="5 mm [THT]"]
  LED8 = LED - 5mm [color="Red (633nm)" current=0.030 package="5 mm [THT]"]
  LED9 = LED - 5mm [color="Red (633nm)" current=0.030 package="5 mm [THT]"]
  J2 = Piezo Speaker
  TEST1 = Pushbutton [package="[THT]"]
  U1 = ESP32S-HiLetgo [part_number=ESP32S-HiLetgo]  # not connected

nets:
  N1: GY-NEO6MV3.RX-I, GY-NEO6MV3.TX-O
  N2: L8.pin_0, SENSITIVITY1.leg2, TEST1.Pin_1, TEST1.Pin_2
  N3: L8.pin_1, L9.pin_0
  N4: L9.pin_1, L10.pin_0
  N5: L10.pin_1, L11.pin_1
  N6: L11.pin_0, L12.pin_1
  N7: L12.pin_0, L13.pin_1
  N8: L13.pin_0, L14.pin_1
  N9: L14.pin_0, VCC2.+, J2.pin2
  N10: S3.pin_1, LED7.cathode, LED8.cathode, LED9.cathode
  N11: S3.pin_2, PWR1.anode, SENSITIVITY1.wiper, TEST1.Pin_3, TEST1.Pin_4
  N12: VCC2.-, R2.Pin_1
  N13: PWR1.cathode, S4.L2
  N14: S4.COM, R2.Pin_0
  N15: LED7.anode, LED8.anode, LED9.anode, J2.pin1

notes:
  GND: Black
  VCC: Red
  RX: Yellow
  TX: Green

custom parts:
  sim800L v2 evb: sim800L v2 evb GSM module.
  ESP32S-HiLetgo: HiLetgo ESP-WROOM-32 ESP32 ESP-32S Development Board 2.4GHz Dual-Mode WiFi + Bluetooth Dual Cores Microcontroller The ESP32 integrated with Antenna switches, RF Balun, power amplifiers, low-noise amplifiers, filters, and management modules, and the entire solution occupies the least area of PCB. 2.4 GHz Wi-Fi plus Bluetooth dual-mode chip, with TSMC Ultra-low power consumption 40nm technology,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
