# Fritzing sketch Motor (saved by Fritzing 0.9.3b)

parts:
  U1 = ESP32S-HiLetgo [part_number=ESP32S-HiLetgo]
  L298N1 = L298N DC motor driver
  M1 = DC Motor  # not connected
  M2 = DC Motor  # not connected
  Part2 = Arduino Uno (Rev3)
  JACK1 = 2.1mm Barrel Jack with Terminal Block

nets:
  N1: U1.GPIO3, Part2.A4/SDA
  N2: U1.GPIO22, Part2.A5/SCL
  N3: L298N1.12V, JACK1.POS
  GND: L298N1.GND, Part2.GND, JACK1.NEG
  N4: L298N1.ENA, Part2.D9_PWM
  N5: L298N1.ENB, Part2.D3_PWM
  N6: L298N1.IN1, Part2.D8
  N7: L298N1.IN2, Part2.D7
  N8: L298N1.IN3, Part2.D5_PWM
  N9: L298N1.IN4, Part2.D4

custom parts:
  ESP32S-HiLetgo: HiLetgo ESP-WROOM-32 ESP32 ESP-32S Development Board 2.4GHz Dual-Mode WiFi + Bluetooth Dual Cores Microcontroller The ESP32 integrated with Antenna switches, RF Balun, power amplifiers, low-noise amplifiers, filters, and management modules, and the entire solution occupies the least area of PCB. 2.4 GHz Wi-Fi plus Bluetooth dual-mode chip, with TSMC Ultra-low power consumption 40nm technology,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
  L298N DC motor driver: 2x DC motor driver with 78M05 positive voltage regulator (7..35 V) L298N: max 46 V, 2 A Set 5 V Enable jumper to enable 5 V regultor (needed for the L298N) and +5 V output at screw terminal or supply external +5 V at screw terminal Set ENA and/or ENB to +5 V to enable motor permanently or supply ENA and/or ENB with PWM signal IN1 and IN2 set rotation directory for motor A (OUT1/OUT2) IN2 and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
